// Logisim project ex4.circ as structural Verilog: 1 circuit, main circuit main
module main (
  input  in_1,
  input  in_2,
  input  in_3,
  input  in_4,
  input  in_5,
  input  in_6,
  output out_7,
  output out_8
);

  wire and_1_out, and_2_out, and_3_out, nand_1_out, nand_2_out, nand_3_out;

  and and_1 (and_1_out, ~in_1, in_3);  // AND_Gate
  and and_2 (and_2_out, ~in_1, in_2);  // AND_Gate
  and and_3 (and_3_out, in_1, ~in_3);  // AND_Gate
  nand nand_1 (nand_1_out, ~in_4, in_6);  // NAND_Gate
  nand nand_2 (nand_2_out, ~in_4, in_5);  // NAND_Gate
  nand nand_3 (nand_3_out, in_4, ~in_6);  // NAND_Gate
  or or_1 (out_7, and_1_out, and_2_out, and_3_out);
  or or_2 (out_8, ~nand_1_out, ~nand_2_out, ~nand_3_out);  // OR_Gate
endmodule
