// Logisim project ex5.circ as structural Verilog: 5 circuits, main circuit main
module main (
  input  [7:0] INPUT0,
  output [2:0] Y,
  output NONE
);

  Y2_logic y2_logic_1 (.INPUT2(INPUT0), .out_2(Y[2]));
  Y1_logic y1_logic_1 (.INPUT1(INPUT0), .out_2(Y[1]));
  Y0_logic y0_logic_1 (.INPUT0(INPUT0), .out_2(Y[0]));
  check_none check_none_1 (.INPUT3(INPUT0), .NONE(NONE));
endmodule

module Y1_logic (
  input  [7:0] INPUT1,
  output out_2
);

  wire and_1_out, and_2_out, or_1_out;

  or or_1 (or_1_out, INPUT1[6], INPUT1[7]);
  and and_1 (and_1_out, INPUT1[2], ~INPUT1[4], ~INPUT1[5]);  // AND_Gate
  and and_2 (and_2_out, INPUT1[3], ~INPUT1[4], ~INPUT1[5]);  // AND_Gate
  or or_2 (out_2, or_1_out, and_1_out, and_2_out);
endmodule

module Y2_logic (
  input  [7:0] INPUT2,
  output out_2
);

  or or_1 (out_2, INPUT2[4], INPUT2[5], INPUT2[6], INPUT2[7]);
endmodule

module Y0_logic (
  input  [7:0] INPUT0,
  output out_2
);

  wire and_1_out, and_2_out, and_3_out;

  and and_1 (and_1_out, INPUT0[1], ~INPUT0[2], ~INPUT0[3], ~INPUT0[4], ~INPUT0[5], ~INPUT0[6], ~INPUT0[7]);  // AND_Gate
  and and_2 (and_2_out, INPUT0[3], ~INPUT0[4], ~INPUT0[5], ~INPUT0[6], ~INPUT0[7]);  // AND_Gate
  and and_3 (and_3_out, INPUT0[5], ~INPUT0[6], ~INPUT0[7]);  // AND_Gate
  or or_1 (out_2, and_1_out, and_2_out, INPUT0[7], and_3_out);
endmodule

module check_none (
  input  [7:0] INPUT3,
  output NONE
);

  and and_1 (NONE, ~INPUT3[0], ~INPUT3[1], ~INPUT3[2], ~INPUT3[3], ~INPUT3[4], ~INPUT3[5], ~INPUT3[6], ~INPUT3[7]);  // AND_Gate
endmodule
